// Digital circuit Bus Control.dig as structural Verilog
module Bus_Control (
  input  [7:0] Main,
  input  [6:0] Xfer_2,
  input  [3:0] Inc,
  input  [3:0] ALU_Assert,
  input  [2:0] Addr_Assert,
  input  Reset,
  output [3:0] GPR_A,
  output [3:0] GPR_B,
  output [3:0] GPR_C,
  output [3:0] GPR_D,
  output [2:0] Const,
  output [7:0] XFER,
  output [3:0] Mem,
  output [6:0] Dev_Assert,
  output [5:0] Dev_Load,
  output [5:0] PCRA2,
  output [5:0] PCRA3,
  output [5:0] SP,
  output [5:0] SI,
  output [5:0] DI,
  output Alu_Assert_2
);

  not not_1 (DI[0], Reset);
  Demultiplexer #(.Selector_Bits(3)) demultiplexer_1 (
    .sel(Xfer_2[6:4]), .in(1'b1), .out_0(Mem[3]), .out_1(PCRA2[5]), .out_2(PCRA3[5]), .out_3(SP[5]),
    .out_4(SI[5]), .out_5(DI[5]), .out_6(XFER[2]), .out_7(XFER[3]));
  Demultiplexer #(.Selector_Bits(3)) demultiplexer_2 (
    .sel(Addr_Assert), .in(1'b1), .out_1(PCRA2[4]), .out_2(PCRA3[4]), .out_3(SP[4]), .out_4(SI[4]),
    .out_5(DI[4]), .out_6(XFER[1]));  // open: out_0, out_7
  Demultiplexer #(.Selector_Bits(2)) demultiplexer_3 (
    .sel(Inc[3:2]), .in(1'b1), .out_1(SP[2]), .out_2(SI[2]), .out_3(DI[2]));  // open: out_0
  Demultiplexer #(.Selector_Bits(2)) demultiplexer_4 (
    .sel(Inc[1:0]), .in(1'b1), .out_0(PCRA2[2]), .out_1(PCRA3[2]));  // open: out_2, out_3
  Demultiplexer #(.Selector_Bits(4)) demultiplexer_5 (
    .sel(Xfer_2[3:0]), .in(1'b1), .out_1(PCRA2[3]), .out_2(PCRA3[3]), .out_3(SP[3]), .out_4(SI[3]),
    .out_5(DI[3]), .out_8(Const[0]), .out_9(PCRA2[1]), .out_10(PCRA3[1]), .out_11(SP[1]), .out_12(SI[1]),
    .out_13(DI[1]), .out_14(XFER[0]));  // open: out_0, out_6, out_7, out_15
  Demultiplexer #(.Selector_Bits(2)) demultiplexer_6 (
    .sel(ALU_Assert[3:2]), .in(1'b1), .out_0(GPR_A[3]), .out_1(GPR_B[3]), .out_2(GPR_C[3]), .out_3(GPR_D[3]));
  Demultiplexer #(.Selector_Bits(2)) demultiplexer_7 (
    .sel(ALU_Assert[1:0]), .in(1'b1), .out_0(GPR_A[2]), .out_1(GPR_B[2]), .out_2(GPR_C[2]), .out_3(GPR_D[2]));
  Demultiplexer #(.Selector_Bits(4)) demultiplexer_8 (
    .sel(Main[3:0]), .in(1'b1), .out_1(GPR_A[1]), .out_2(GPR_B[1]), .out_3(GPR_C[1]), .out_4(GPR_D[1]),
    .out_5(Const[2]), .out_6(XFER[5]), .out_7(XFER[7]), .out_8(Alu_Assert_2), .out_9(Dev_Assert[0]),
    .out_10(Dev_Assert[1]), .out_11(Dev_Assert[2]), .out_12(Dev_Assert[3]), .out_13(Dev_Assert[4]),
    .out_14(Dev_Assert[5]), .out_15(Mem[0]));  // open: out_0
  Demultiplexer #(.Selector_Bits(4)) demultiplexer_9 (
    .sel(Main[7:4]), .in(1'b1), .out_1(GPR_A[0]), .out_2(GPR_B[0]), .out_3(GPR_C[0]), .out_4(GPR_D[0]),
    .out_5(Const[1]), .out_6(XFER[4]), .out_7(XFER[6]), .out_9(Dev_Load[0]), .out_10(Dev_Load[1]),
    .out_11(Dev_Load[2]), .out_12(Dev_Load[3]), .out_13(Dev_Load[4]), .out_14(Dev_Load[5]), .out_15(Mem[1]));  // open: out_0, out_8
  and and_1 (Mem[2], Main[5], Main[4], Main[6], Main[7]);
  // Pins of 6 and 7 bits meet at Dev_Assert

  assign PCRA2[0] = DI[0];
  assign PCRA3[0] = DI[0];
  assign SI[0] = DI[0];
  assign SP[0] = DI[0];

  // Other names for the same wires on the sheet: Alu_Assert_t = Alu_Assert_2

  // Notes on the sheet:
  //   GPR_A: 0: Load
  //   1: Assert Main
  //   2: Assert LHS
  //   3: Assert RHS
  //   GPR_B: 0: Load
  //   1: Assert Main
  //   2: Assert LHS
  //   3: Assert RHS
  //   GPR_C: 0: Load
  //   1: Assert Main
  //   2: Assert LHS
  //   3: Assert RHS
  //   GPR_D: 0: Load
  //   1: Assert Main
  //   2: Assert LHS
  //   3: Assert RHS
  //   Const: 0: Load Bus
  //   1: Load Mem
  //   2: Assert Main
  //   XFER: 0: RegTX Load
  //   1: RegTX Assert Addr
  //   2: RegTX Assert Xfer
  //   3: RegTX Assert Mode
  //   4: RegTL Load
  //   5: RegTL Assert
  //   6: RegTH Load
  //   7: RegTH Assert
  //   Mem: 0: Assert
  //   1: Load
  //   2: Dir
  //   3: Ack
  //   Main: 0-3: Assert A-D
  //   4-7: Load A-D
  //   Xfer_2: Assert:
  //   000xxxx: -
  //   001xxxx: PCRA0
  //   010xxxx: PCRA1
  //   011xxxx: SP
  //   100xxxx: SI
  //   101xxxx: DI
  //   110xxxx: TX
  //   111xxxx: TX mode
  //   Load:
  //   xxx0000: -
  //   xxx0001: PCRA0
  //   xxx0010: PCRA1
  //   xxx0011: SP
  //   xxx0100: SI
  //   xxx0101: DI
  //   xxx0110: TX
  //   xxx0111: -
  //   xxx1000: Const LoadMem
  //   Dec:
  //   x1001: PCRA0
  //   x1010: PCRA1
  //   x1011: SP
  //   x1100: SI
  //   x1101: DI
  //   x1110: -
  //   x1111: -
  //   Inc: xx00: Inc PCRA0
  //   xx01: Inc PCRA1
  //   xx10: -
  //   xx11: -
  //   00xx: -
  //   01xx: Inc SP
  //   10xx: Inc SI
  //   11xx: Inc DI
  //   ALU_Assert: xx00-xx11: LHS A-B
  //   00xx-11xx: RHS A-B
  //   Addr_Assert: 000 Memory Ack
  //   001 PCRA0
  //   010 PCRA1
  //   011 SP
  //   100 SI
  //   101 DI
  //   111 TX
  //   Dev_Assert: 0: ALU
  //   1-6: Assert Dev 9-14
  //   Dev_Load: 0-5: Load Dev 9-14
  //   PCRA2: 0: Clock
  //   1: Clear
  //   2: Dec
  //   3: Inc
  //   4: Load
  //   5: Assert Addr
  //   6: Assert Bus
  //   PCRA3: 0: Clock
  //   1: Clear
  //   2: Dec
  //   3: Inc
  //   4: Load
  //   5: Assert Addr
  //   6: Assert Bus
  //   SP: 0: Clock
  //   1: Clear
  //   2: Dec
  //   3: Inc
  //   4: Load
  //   5: Assert Addr
  //   6: Assert Bus
  //   SI: 0: Clock
  //   1: Clear
  //   2: Dec
  //   3: Inc
  //   4: Load
  //   5: Assert Addr
  //   6: Assert Bus
  //   DI: 0: Clock
  //   1: Clear
  //   2: Dec
  //   3: Inc
  //   4: Load
  //   5: Assert Addr
  //   6: Assert Bus
  //   Alu_Assert_2: 0: ALU
  //   1-6: Assert Dev 9-14
endmodule
