// Digital circuit Core.dig as structural Verilog
module Core (
  input  Clock,
  input  nReset,
  input  [7:0] D_IN,
  output R_nW,
  output [15:0] Addr,
  output [7:0] D_OUT
);

  wire Break, BusRequest, decoder_1_out_0, decoder_1_out_1, decoder_2_out_1, decoder_2_out_2,
       decoder_2_out_3, decoder_2_out_4, decoder_2_out_5, decoder_2_out_7, decoder_2_out_8, decoder_2_out_9,
       decoder_2_out_10, decoder_2_out_11, decoder_2_out_12, decoder_2_out_13, decoder_2_out_14,
       decoder_2_out_15, decoder_3_out_1, decoder_3_out_2, decoder_3_out_3, FetchSuppress, LoadTH, LoadTL,
       LoadTX, not_1_out, or_1_out, or_2_out, or_3_out, or_4_out, or_5_out, PCRAFlip, SelGPRs;
  wire [1:0] Assert2Main, demultiplexer_1_out_0, demultiplexer_1_out_1, Inc, LoadMain;
  wire [2:0] AddrAssert, Assert2Xfer;
  wire [3:0] AluAssert, AluOp, LoadXfer_Dec;
  wire [4:0] AluFlags;
  wire [7:0] ALU_p6, GPRs_da, GPRs_db, MemData, multiplexer_2_out, register_1_q, register_3_q, Xfer_d_th,
       Xfer_d_tl;
  wire [7:2] register_4_q;
  wire [15:0] _1A_d, _2A_d, DI_out, PCRA0_out, PCRA1_out, SI_out, SP_out, Xfer, Xfer_d_tx;

  Decoder #(.Selector_Bits(2)) decoder_1 (
    .sel({BusRequest, PCRAFlip}), .out_0(decoder_1_out_0), .out_1(decoder_1_out_1));  // open: out_2, out_3
  Decoder #(.Selector_Bits(4)) decoder_2 (
    .sel(LoadXfer_Dec), .out_1(decoder_2_out_1), .out_2(decoder_2_out_2), .out_3(decoder_2_out_3),
    .out_4(decoder_2_out_4), .out_5(decoder_2_out_5), .out_6(LoadTX), .out_7(decoder_2_out_7),
    .out_8(decoder_2_out_8), .out_9(decoder_2_out_9), .out_10(decoder_2_out_10), .out_11(decoder_2_out_11),
    .out_12(decoder_2_out_12), .out_13(decoder_2_out_13), .out_14(decoder_2_out_14), .out_15(decoder_2_out_15));  // open: out_0
  Decoder #(.Selector_Bits(2)) decoder_3 (
    .sel(Inc), .out_1(decoder_3_out_1), .out_2(decoder_3_out_2), .out_3(decoder_3_out_3));  // open: out_0
  or or_1 (or_1_out, decoder_1_out_0, decoder_2_out_9);
  or or_2 (or_2_out, decoder_1_out_1, decoder_2_out_10);
  or or_3 (or_3_out, decoder_3_out_1, decoder_2_out_11);
  or or_4 (or_4_out, decoder_3_out_2, decoder_2_out_12);
  or or_5 (or_5_out, decoder_3_out_3, decoder_2_out_13);
  CounterPreset #(.Bits(16)) PCRA0 (
    .en(or_1_out), .C(not_1_out), .dir(decoder_2_out_9), .in(Xfer), .ld(decoder_2_out_1), .clr(nReset),
    .out(PCRA0_out));  // open: ovf
  CounterPreset #(.Bits(16)) PCRA1 (
    .en(or_2_out), .C(not_1_out), .dir(decoder_2_out_10), .in(Xfer), .ld(decoder_2_out_2), .clr(nReset),
    .out(PCRA1_out));  // open: ovf
  CounterPreset #(.Bits(16)) SP (
    .en(or_3_out), .C(not_1_out), .dir(decoder_2_out_11), .in(Xfer), .ld(decoder_2_out_3), .clr(nReset),
    .out(SP_out));  // open: ovf
  CounterPreset #(.Bits(16)) SI (
    .en(or_4_out), .C(not_1_out), .dir(decoder_2_out_12), .in(Xfer), .ld(decoder_2_out_4), .clr(nReset),
    .out(SI_out));  // open: ovf
  CounterPreset #(.Bits(16)) DI (
    .en(or_5_out), .C(not_1_out), .dir(decoder_2_out_13), .in(Xfer), .ld(decoder_2_out_5), .clr(nReset),
    .out(DI_out));  // open: ovf
  not not_1 (not_1_out, Clock);
  Multiplexer #(.Selector_Bits(3), .Bits(16)) multiplexer_1 (
    .sel(AddrAssert), .in_0({16{1'b0}}), .in_1(PCRA0_out), .in_2(PCRA1_out), .in_3(SP_out), .in_4(SI_out),
    .in_5(DI_out), .in_6(Xfer_d_tx), .in_7({16{1'b0}}), .out(Addr));
  Register #(.Bits(8)) register_1 (.D(MemData), .C(Clock), .en(1'b1), .Q(register_1_q));
  mem_io mem_io_1 (.D_IN(D_OUT), .Addr(Addr), .R_nW(R_nW), .Clock(Clock), .D_OUT(MemData));
  Register #(.Bits(16)) register_2 (
    .D(_1A_d), .C(Clock), .en(1'b1), .Q({FetchSuppress, Assert2Xfer, LoadXfer_Dec, AluOp, AluAssert}));
  ROM #(.AddrBits(15), .Bits(8)) _1A (.A({nReset, PCRAFlip, AluFlags, multiplexer_2_out}), .sel(1'b1), .D(_1A_d[7:0]));
  Multiplexer #(.Selector_Bits(2), .Bits(8)) multiplexer_2 (
    .sel({BusRequest, FetchSuppress}), .in_0(MemData), .in_1({8{1'b0}}), .in_2({8{1'b0}}),
    .in_3(register_1_q), .out(multiplexer_2_out));
  Multiplexer #(.Selector_Bits(3), .Bits(16)) multiplexer_3 (
    .sel(Assert2Xfer), .in_0({16{1'b0}}), .in_1(PCRA0_out), .in_2(PCRA1_out), .in_3(SP_out), .in_4(SI_out),
    .in_5(DI_out), .in_6(Xfer_d_tx), .in_7({16{1'b0}}), .out(Xfer));
  ROM #(.AddrBits(15), .Bits(8)) _1B (.A({nReset, PCRAFlip, AluFlags, multiplexer_2_out}), .sel(1'b1), .D(_1A_d[15:8]));
  Register #(.Bits(8)) register_3 (.D(multiplexer_2_out), .C(Clock), .en(1'b1), .Q(register_3_q));
  Register #(.Bits(16)) register_4 (
    .D(_2A_d), .C(Clock), .en(1'b1),
    .Q({Break, PCRAFlip, BusRequest, AddrAssert, Inc, register_4_q[7], SelGPRs, LoadMain, register_4_q[3:2], Assert2Main}));
  ROM #(.AddrBits(15), .Bits(8)) _2A (.A({nReset, PCRAFlip, AluFlags, register_3_q}), .sel(1'b1), .D(_2A_d[7:0]));
  Decoder #(.Selector_Bits(2)) decoder_4 (
    .sel(demultiplexer_1_out_0), .out_1(R_nW), .out_2(LoadTL), .out_3(LoadTH));  // open: out_0
  ROM #(.AddrBits(15), .Bits(8)) _2B (.A({nReset, PCRAFlip, AluFlags, register_3_q}), .sel(1'b1), .D(_2A_d[15:8]));
  Demultiplexer #(.Bits(2)) demultiplexer_1 (
    .sel(SelGPRs), .in(LoadMain), .out_0(demultiplexer_1_out_0), .out_1(demultiplexer_1_out_1));
  // Probe P2 on register_3_q
  // Probe P1 on multiplexer_2_out
  // Probe Flags on {nReset, PCRAFlip, AluFlags}
  RegisterFile #(.Bits(8)) GPRs (
    .Din(D_OUT), .we(SelGPRs), .Rw(demultiplexer_1_out_1), .C(not_1_out), .Ra(AluAssert[1:0]),
    .Rb(AluAssert[3:2]), .Da(GPRs_da), .Db(GPRs_db));
  TransferRegister u_Xfer (
    .L_TL(LoadTL), .L_TH(LoadTH), .L_TX(LoadTX), .D_IN(D_OUT), .X_IN(Xfer), .C(not_1_out), .D_TH(Xfer_d_th),
    .D_TL(Xfer_d_tl), .D_TX(Xfer_d_tx));
  // ALU ALU: pin names not known; wires that end beside it: GPRs_da, GPRs_db, AluOp, not_1_out, AluFlags, ALU_p6
  Multiplexer #(.Selector_Bits(2), .Bits(8)) multiplexer_4 (
    .sel(Assert2Main), .in_0(ALU_p6), .in_1(Xfer_d_th), .in_2(Xfer_d_tl), .in_3(MemData), .out(D_OUT));
  // Probe on Assert2Xfer
  // Probe on LoadXfer_Dec
  // Probe Mem on MemData
  // Probe Main on D_OUT
  // Probe Addr on Addr
  // Probe Xfer on Xfer

  // Other names for the same wires on the sheet: Main[7:0] = D_OUT; Reset = nReset

  // Notes on the sheet:
  //   Clock: Hz: 1000
  //   nReset: default 1
  //   contents of _1A (hex, n*v repeats v):
  //   0,0,0,0,0,0,0,0,0,0,0,0,0,0,0,0,0,0,0,0,0,0,0,0,0,0,0,0,0,0,0,0,0,0,0,0,0,0,0,0,0,
  //   0,0,0,0,0,0,0,0,0,0,0,0,0,0,0,0,0,0,0,0,0,0,0,0,0,0,0,0,0,0,0,0,0,0,0,0,0,0,0,0,0,
  //   0,0,0,0,0,0,0,0,0,0,0,0,0,0,0,0,0,0,0,0,0,0,0,0,0,0,0,0,0,0,0,0,0,0,0,0,0,0,0,0,0,
  //   0,0,0,0,e0,10,15,1a,1f,20,25,2a,2f,34,38,3c,31,39,3d,32,36,3e,33,37,3b,44,48,4c,41,
  //   49,4d,42,46,4e,43,47,4b,50,55,5a,5f,60,65,6a,6f,74,78,7c,71,79,7d,72,76,7e,73,77,
  //   7b,84,88,8c,81,89,8d,82,86,8e,83,87,8b,90,95,9a,9f,a4,a8,ac,a1,a9,ad,a2,a6,ae,a3,
  //   a7,ab,b4,b8,bc,b1,b9,bd,b2,b6,be,b3,b7,bb,c4,c8,cc,c1,c9,cd,c2,c6,ce,c3,c7,cb,c0,
  //   c5,ca,cf,d0,d5,da,df,74,78,7c,71,79,7d,72,76,7e,73,77,7b,a0,a5,aa,af,0,0,0,0,0,0,
  //   0,0,0,0,0,0,0,0,0,0,0,0,0,0,0,0,0,0,0,0,0,0,0,0,0,0,0,0,0,0,0,0,0,0,0,0,0,0,0,0,0,
  //   0,0,0,0,0,0,0,0,0,0,0,0,0,0,0,0,0,0,0,0,0,0,0,0,0,0,0,0,0,0,0,0,0,0,0,0,0,0,0,0,0,
  //   0,0,0,0,0,0,0,0,0,0,0,0,0,0,0,0,0,0,0,0,0,0,0,0,0,0,0,0,0,0,0,0,0,0,0,0,0,0,0,e0,
  //   10,15,1a,1f,20,25,2a,2f,34,38,3c,31,39,3d,32,36,3e,33,37,3b,44,48,4c,41,49,4d,42,
  //   46,4e,43,47,4b,50,55,5a,5f,60,65,6a,6f,74,78,7c,71,79,7d,72,76,7e,73,77,7b,84,88,
  //   8c,81,89,8d,82,86,8e,83,87,8b,90,95,9a,9f,a4,a8,ac,a1,a9,ad,a2,a6,ae,a3,a7,ab,b4,
  //   b8,bc,b1,b9,bd,b2,b6,be,b3,b7,bb,c4,c8,cc,c1,c9,cd,c2,c6,ce,c3,c7,cb,c0,c5,ca,cf,
  //   d0,d5,da,df,74,78,7c,71,79,7d,72,76,7e,73,77,7b,a0,a5,aa,af,0,0,0,0,0,0,0,0,0,0,0,
  //   0,0,0,0,0,0,0,0,0,0,0,0,0,0,0,0,0,0,0,0,0,0,0,0,0,0,0,0,0,0,0,0,0,0,0,0,0,0,0,0,0,
  //   0,0,0,0,0,0,0,0,0,0,0,0,0,0,0,0,0,0,0,0,0,0,0,0,0,0,0,0,0,0,0,0,0,0,0,0,0,0,0,0,0,
  //   0,0,0,0,0,0,0,0,0,0,0,0,0,0,0,0,0,0,0,0,0,0,0,0,0,0,0,0,0,0,0,0,0,0,e0,10,15,1a,1f,
  //   20,25,2a,2f,34,38,3c,31,39,3d,32,36,3e,33,37,3b,44,48,4c,41,49,4d,42,46,4e,43,47,
  //   4b,50,55,5a,5f,60,65,6a,6f,74,78,7c,71,79,7d,72,76,7e,73,77,7b,84,88,8c,81,89,8d,
  //   82,86,8e,83,87,8b,90,95,9a,9f,a4,a8,ac,a1,a9,ad,a2,a6,ae,a3,a7,ab,b4,b8,bc,b1,b9,
  //   bd,b2,b6,be,b3,b7,bb,c4,c8,cc,c1,c9,cd,c2,c6,ce,c3,c7,cb,c0,c5,ca,cf,d0,d5,da,df,
  //   74,78,7c,71,79,7d,72,76,7e,73,77,7b,a0,a5,aa,af,0,0,0,0,0,0,0,0,0,0,0,0,0,0,0,0,0,
  //   0,0,0,0,0,0,0,0,0,0,0,0,0,0,0,0,0,0,0,0,0,0,0,0,0,0,0,0,0,0,0,0,0,0,0,0,0,0,0,0,0,
  //   0,0,0,0,0,0,0,0,0,0,0,0,0,0,0,0,0,0,0,0,0,0,0,0,0,0,0,0,0,0,0,0,0,0,0,0,0,0,0,0,0,
  //   0,0,0,0,0,0,0,0,0,0,0,0,0,0,0,0,0,0,0,0,0,0,0,0,0,0,0,0,e0,10,15,1a,1f,20,25,2a,2f,
  //   34,38,3c,31,39,3d,32,36,3e,33,37,3b,44,48,4c,41,49,4d,42,46,4e,43,47,4b,50,55,5a,
  //   5f,60,65,6a,6f,74,78,7c,71,79,7d,72,76,7e,73,77,7b,84,88,8c,81,89,8d,82,86,8e,83,
  //   87,8b,90,95,9a,9f,a4,a8,ac,a1,a9,ad,a2,a6,ae,a3,a7,ab,b4,b8,bc,b1,b9,bd,b2,b6,be,
  //   b3,b7,bb,c4,c8,cc,c1,c9,cd,c2,c6,ce,c3,c7,cb,c0,c5,ca,cf,d0,d5,da,df,74,78,7c,71,
  //   79,7d,72,76,7e,73,77,7b,a0,a5,aa,af,0,0,0,0,0,0,0,0,0,0,0,0,0,0,0,0,0,0,0,0,0,0,0,
  //   0,0,0,0,0,0,0,0,0,0,0,0,0,0,0,0,0,0,0,0,0,0,0,0,0,0,0,0,0,0,0,0,0,0,0,0,0,0,0,0,0,
  //   0,0,0,0,0,0,0,0,0,0,0,0,0,0,0,0,0,0,0,0,0,0,0,0,0,0,0,0,0,0,0,0,0,0,0,0,0,0,0,0,0,
  //   0,0,0,0,0,0,0,0,0,0,0,0,0,0,0,0,0,0,0,0,0,0,e0,10,15,1a,1f,20,25,2a,2f,34,38,3c,31,
  //   39,3d,32,36,3e,33,37,3b,44,48,4c,41,49,4d,42,46,4e,43,47,4b,50,55,5a,5f,60,65,6a,
  //   6f,74,78,7c,71,79,7d,72,76,7e,73,77,7b,84,88,8c,81,89,8d,82,86,8e,83,87,8b,90,95,
  //   9a,9f,a4,a8,ac,a1,a9,ad,a2,a6,ae,a3,a7,ab,b4,b8,bc,b1,b9,bd,b2,b6,be,b3,b7,bb,c4,
  //   c8,cc,c1,c9,cd,c2,c6,ce,c3,c7,cb,c0,c5,ca,cf,d0,d5,da,df,74,78,7c,71,79,7d,72,76,
  //   7e,73,77,7b,a0,a5,aa,af,0,0,0,0,0,0,0,0,0,0,0,0,0,0,0,0,0,0,0,0,0,0,0,0,0,0,0,0,0,
  //   0,0,0,0,0,0,0,0,0,0,0,0,0,0,0,0,0,0,0,0,0,0,0,0,0,0,0,0,0,0,0,0,0,0,0,0,0,0,0,0,0,
  //   0,0,0,0,0,0,0,0,0,0,0,0,0,0,0,0,0,0,0,0,0,0,0,0,0,0,0,0,0,0,0,0,0,0,0,0,0,0,0,0,0,
  //   0,0,0,0,0,0,0,0,0,0,0,0,0,0,0,0,e0,10,15,1a,1f,20,25,2a,2f,34,38,3c,31,39,3d,32,36,
  //   3e,33,37,3b,44,48,4c,41,49,4d,42,46,4e,43,47,4b,50,55,5a,5f,60,65,6a,6f,74,78,7c,
  //   71,79,7d,72,76,7e,73,77,7b,84,88,8c,81,89,8d,82,86,8e,83,87,8b,90,95,9a,9f,a4,a8,
  //   ac,a1,a9,ad,a2,a6,ae,a3,a7,ab,b4,b8,bc,b1,b9,bd,b2,b6,be,b3,b7,bb,c4,c8,cc,c1,c9,
  //   cd,c2,c6,ce,c3,c7,cb,c0,c5,ca,cf,d0,d5,da,df,74,78,7c,71,79,7d,72,76,7e,73,77,7b,
  //   a0,a5,aa,af,0,0,0,0,0,0,0,0,0,0,0,0,0,0,0,0,0,0,0,0,0,0,0,0,0,0,0,0,0,0,0,0,0,0,0,
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  //   contents of _1B (hex, n*v repeats v):
  //   0,80,80,80,80,80,80,0,0,0,0,0,0,0,0,0,0,0,0,0,0,0,0,0,0,0,0,0,0,0,0,0,0,0,0,62,26,
  //   63,36,64,46,65,56,45,54,34,35,0,a,b,c,d,0,0,0,0,0,0,0,0,0,0,0,0,0,0,0,0,0,0,0,0,0,
  //   0,0,0,0,0,0,0,0,0,0,0,0,0,0,0,0,0,0,0,62,52,0,0,61,0,61,0,61,0,61,0,61,0,61,0,61,
  //   0,61,0,61,51,b,b,b,b,b,b,0,0,0,0,0,0,0,0,0,0,0,0,0,0,0,0,0,0,0,0,0,0,0,0,0,0,0,0,
  //   0,0,0,0,0,0,0,0,0,0,0,0,0,0,0,0,0,0,0,0,0,0,0,0,0,0,0,0,0,0,0,0,0,0,0,0,0,0,0,0,0,
  //   0,0,0,0,0,0,0,0,0,0,0,0,0,0,0,0,0,0,0,0,0,0,0,0,0,0,0,0,0,0,0,0,0,0,0,0,0,0,0,0,0,
  //   0,0,0,0,0,0,0,0,0,0,0,0,0,0,0,0,0,0,0,0,0,0,0,0,0,0,0,80,80,80,80,80,80,0,0,0,0,0,
  //   0,0,0,0,0,0,0,0,0,0,0,0,0,0,0,0,0,0,0,0,0,0,0,62,26,63,36,64,46,65,56,45,54,34,35,
  //   0,a,b,c,d,0,0,0,0,0,0,0,0,0,0,0,0,0,0,0,0,0,0,0,0,0,0,0,0,0,0,0,0,0,0,0,0,0,0,0,0,
  //   0,0,0,0,62,52,0,0,61,61,0,0,61,0,61,0,61,0,61,61,0,61,61,0,61,51,b,b,b,b,b,b,0,0,
  //   0,0,0,0,0,0,0,0,0,0,0,0,0,0,0,0,0,0,0,0,0,0,0,0,0,0,0,0,0,0,0,0,0,0,0,0,0,0,0,0,0,
  //   0,0,0,0,0,0,0,0,0,0,0,0,0,0,0,0,0,0,0,0,0,0,0,0,0,0,0,0,0,0,0,0,0,0,0,0,0,0,0,0,0,
  //   0,0,0,0,0,0,0,0,0,0,0,0,0,0,0,0,0,0,0,0,0,0,0,0,0,0,0,0,0,0,0,0,0,0,0,0,0,0,0,0,0,
  //   0,0,0,0,0,0,0,0,0,0,0,0,80,80,80,80,80,80,0,0,0,0,0,0,0,0,0,0,0,0,0,0,0,0,0,0,0,0,
  //   0,0,0,0,0,0,0,0,62,26,63,36,64,46,65,56,45,54,34,35,0,a,b,c,d,0,0,0,0,0,0,0,0,0,0,
  //   0,0,0,0,0,0,0,0,0,0,0,0,0,0,0,0,0,0,0,0,0,0,0,0,0,0,0,0,0,0,62,52,0,0,61,0,61,61,
  //   0,0,61,0,61,0,61,61,0,61,0,0,61,51,b,b,b,b,b,b,0,0,0,0,0,0,0,0,0,0,0,0,0,0,0,0,0,
  //   0,0,0,0,0,0,0,0,0,0,0,0,0,0,0,0,0,0,0,0,0,0,0,0,0,0,0,0,0,0,0,0,0,0,0,0,0,0,0,0,0,
  //   0,0,0,0,0,0,0,0,0,0,0,0,0,0,0,0,0,0,0,0,0,0,0,0,0,0,0,0,0,0,0,0,0,0,0,0,0,0,0,0,0,
  //   0,0,0,0,0,0,0,0,0,0,0,0,0,0,0,0,0,0,0,0,0,0,0,0,0,0,0,0,0,0,0,0,0,0,0,0,0,0,80,80,
  //   80,80,80,80,0,0,0,0,0,0,0,0,0,0,0,0,0,0,0,0,0,0,0,0,0,0,0,0,0,0,0,0,62,26,63,36,64,
  //   46,65,56,45,54,34,35,0,a,b,c,d,0,0,0,0,0,0,0,0,0,0,0,0,0,0,0,0,0,0,0,0,0,0,0,0,0,
  //   0,0,0,0,0,0,0,0,0,0,0,0,0,0,0,62,52,0,0,61,61,0,61,0,0,61,0,61,0,61,0,61,0,0,0,61,
  //   51,b,b,b,b,b,b,0,0,0,0,0,0,0,0,0,0,0,0,0,0,0,0,0,0,0,0,0,0,0,0,0,0,0,0,0,0,0,0,0,
  //   0,0,0,0,0,0,0,0,0,0,0,0,0,0,0,0,0,0,0,0,0,0,0,0,0,0,0,0,0,0,0,0,0,0,0,0,0,0,0,0,0,
  //   0,0,0,0,0,0,0,0,0,0,0,0,0,0,0,0,0,0,0,0,0,0,0,0,0,0,0,0,0,0,0,0,0,0,0,0,0,0,0,0,0,
  //   0,0,0,0,0,0,0,0,0,0,0,0,0,0,0,0,0,0,0,0,0,0,80,80,80,80,80,80,0,0,0,0,0,0,0,0,0,0,
  //   0,0,0,0,0,0,0,0,0,0,0,0,0,0,0,0,0,0,62,26,63,36,64,46,65,56,45,54,34,35,0,a,b,c,d,
  //   0,0,0,0,0,0,0,0,0,0,0,0,0,0,0,0,0,0,0,0,0,0,0,0,0,0,0,0,0,0,0,0,0,0,0,0,0,0,0,0,62,
  //   52,0,0,61,0,61,0,61,61,0,0,61,61,0,0,61,61,0,0,61,51,b,b,b,b,b,b,0,0,0,0,0,0,0,0,
  //   0,0,0,0,0,0,0,0,0,0,0,0,0,0,0,0,0,0,0,0,0,0,0,0,0,0,0,0,0,0,0,0,0,0,0,0,0,0,0,0,0,
  //   0,0,0,0,0,0,0,0,0,0,0,0,0,0,0,0,0,0,0,0,0,0,0,0,0,0,0,0,0,0,0,0,0,0,0,0,0,0,0,0,0,
  //   0,0,0,0,0,0,0,0,0,0,0,0,0,0,0,0,0,0,0,0,0,0,0,0,0,0,0,0,0,0,0,0,0,0,0,0,0,0,0,0,0,
  //   0,0,0,0,0,0,80,80,80,80,80,80,0,0,0,0,0,0,0,0,0,0,0,0,0,0,0,0,0,0,0,0,0,0,0,0,0,0,
  //   0,0,62,26,63,36,64,46,65,56,45,54,34,35,0,a,b,c,d,0,0,0,0,0,0,0,0,0,0,0,0,0,0,0,0,
  //   0,0,0,0,0,0,0,0,0,0,0,0,0,0,0,0,0,0,0,0,0,0,0,0,62,52,0,0,61,61,0,0,61,61,0,0,61,
  //   61,0,61,0,61,0,0,61,51,b,b,b,b,b,b,0,0,0,0,0,0,0,0,0,0,0,0,0,0,0,0,0,0,0,0,0,0,0,
  //   0,0,0,0,0,0,0,0,0,0,0,0,0,0,0,0,0,0,0,0,0,0,0,0,0,0,0,0,0,0,0,0,0,0,0,0,0,0,0,0,0,
  //   0,0,0,0,0,0,0,0,0,0,0,0,0,0,0,0,0,0,0,0,0,0,0,0,0,0,0,0,0,0,0,0,0,0,0,0,0,0,0,0,0,
  //   0,0,0,0,0,0,0,0,0,0,0,0,0,0,0,0,0,0,0,0,0,0,0,0,0,0,0,0,0,0,0,0,80,80,80,80,80,80,
  //   0,0,0,0,0,0,0,0,0,0,0,0,0,0,0,0,0,0,0,0,0,0,0,0,0,0,0,0,62,26,63,36,64,46,65,56,45,
  //   54,34,35,0,a,b,c,d,0,0,0,0,0,0,0,0,0,0,0,0,0,0,0,0,0,0,0,0,0,0,0,0,0,0,0,0,0,0,0,
  //   0,0,0,0,0,0,0,0,0,62,52,0,0,61,0,61,61,0,61,0,0,61,61,0,61,0,61,0,0,61,51,b,b,b,b,
  //   b,b,0,0,0,0,0,0,0,0,0,0,0,0,0,0,0,0,0,0,0,0,0,0,0,0,0,0,0,0,0,0,0,0,0,0,0,0,0,0,0,
  //   0,0,0,0,0,0,0,0,0,0,0,0,0,0,0,0,0,0,0,0,0,0,0,0,0,0,0,0,0,0,0,0,0,0,0,0,0,0,0,0,0,
  //   0,0,0,0,0,0,0,0,0,0,0,0,0,0,0,0,0,0,0,0,0,0,0,0,0,0,0,0,0,0,0,0,0,0,0,0,0,0,0,0,0,
  //   0,0,0,0,0,0,0,0,0,0,0,0,0,0,0,0,80,80,80,80,80,80,0,0,0,0,0,0,0,0,0,0,0,0,0,0,0,0,
  //   0,0,0,0,0,0,0,0,0,0,0,0,62,26,63,36,64,46,65,56,45,54,34,35,0,a,b,c,d,0,0,0,0,0,0,
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  //   contents of _2A (hex, n*v repeats v):
  //   0,43,53,63,73,23,33,40,40,40,50,50,50,60,60,60,70,70,70,20,20,20,20,30,30,30,30,41,
  //   51,61,71,42,52,62,72,0,0,0,0,0,0,0,0,0,0,0,0,0,0,0,0,0,0,0,0,0,0,0,0,0,0,0,0,0,43,
  //   53,63,73,43,53,63,73,43,53,63,73,10,10,10,10,10,10,10,10,10,10,10,10,0,0,0,43,0,0,
  //   0,0,0,0,0,0,0,0,0,0,0,0,0,0,0,0,0,0,0,0,10,10,10,10,11,12,43,53,63,73,23,33,10,0,
  //   40,50,60,70,40,50,60,70,40,40,40,50,50,50,60,60,60,70,70,70,40,40,40,50,50,50,60,
  //   60,60,70,70,70,40,50,60,70,40,50,60,70,40,40,40,50,50,50,60,60,60,70,70,70,40,40,
  //   40,50,50,50,60,60,60,70,70,70,40,50,60,70,40,40,40,50,50,50,60,60,60,70,70,70,40,
  //   40,40,50,50,50,60,60,60,70,70,70,40,40,40,50,50,50,60,60,60,70,70,70,40,50,60,70,
  //   40,50,60,70,0,0,0,0,0,0,0,0,0,0,0,0,0,0,0,0,0,43,53,63,73,23,33,40,40,40,50,50,50,
  //   60,60,60,70,70,70,20,20,20,20,30,30,30,30,41,51,61,71,42,52,62,72,0,0,0,0,0,0,0,0,
  //   0,0,0,0,0,0,0,0,0,0,0,0,0,0,0,0,0,0,0,0,0,43,53,63,73,43,53,63,73,43,53,63,73,10,
  //   10,10,10,10,10,10,10,10,10,10,10,0,0,0,43,0,0,0,0,0,0,0,0,0,0,0,0,0,0,0,0,0,0,0,0,
  //   0,0,10,10,10,10,11,12,43,53,63,73,23,33,10,0,40,50,60,70,40,50,60,70,40,40,40,50,
  //   50,50,60,60,60,70,70,70,40,40,40,50,50,50,60,60,60,70,70,70,40,50,60,70,40,50,60,
  //   70,40,40,40,50,50,50,60,60,60,70,70,70,40,40,40,50,50,50,60,60,60,70,70,70,40,50,
  //   60,70,40,40,40,50,50,50,60,60,60,70,70,70,40,40,40,50,50,50,60,60,60,70,70,70,40,
  //   40,40,50,50,50,60,60,60,70,70,70,40,50,60,70,40,50,60,70,0,0,0,0,0,0,0,0,0,0,0,0,
  //   0,0,0,0,0,43,53,63,73,23,33,40,40,40,50,50,50,60,60,60,70,70,70,20,20,20,20,30,30,
  //   30,30,41,51,61,71,42,52,62,72,0,0,0,0,0,0,0,0,0,0,0,0,0,0,0,0,0,0,0,0,0,0,0,0,0,0,
  //   0,0,0,43,53,63,73,43,53,63,73,43,53,63,73,10,10,10,10,10,10,10,10,10,10,10,10,0,0,
  //   0,43,0,0,0,0,0,0,0,0,0,0,0,0,0,0,0,0,0,0,0,0,0,0,10,10,10,10,11,12,43,53,63,73,23,
  //   33,10,0,40,50,60,70,40,50,60,70,40,40,40,50,50,50,60,60,60,70,70,70,40,40,40,50,50,
  //   50,60,60,60,70,70,70,40,50,60,70,40,50,60,70,40,40,40,50,50,50,60,60,60,70,70,70,
  //   40,40,40,50,50,50,60,60,60,70,70,70,40,50,60,70,40,40,40,50,50,50,60,60,60,70,70,
  //   70,40,40,40,50,50,50,60,60,60,70,70,70,40,40,40,50,50,50,60,60,60,70,70,70,40,50,
  //   60,70,40,50,60,70,0,0,0,0,0,0,0,0,0,0,0,0,0,0,0,0,0,43,53,63,73,23,33,40,40,40,50,
  //   50,50,60,60,60,70,70,70,20,20,20,20,30,30,30,30,41,51,61,71,42,52,62,72,0,0,0,0,0,
  //   0,0,0,0,0,0,0,0,0,0,0,0,0,0,0,0,0,0,0,0,0,0,0,0,43,53,63,73,43,53,63,73,43,53,63,
  //   73,10,10,10,10,10,10,10,10,10,10,10,10,0,0,0,43,0,0,0,0,0,0,0,0,0,0,0,0,0,0,0,0,0,
  //   0,0,0,0,0,10,10,10,10,11,12,43,53,63,73,23,33,10,0,40,50,60,70,40,50,60,70,40,40,
  //   40,50,50,50,60,60,60,70,70,70,40,40,40,50,50,50,60,60,60,70,70,70,40,50,60,70,40,
  //   50,60,70,40,40,40,50,50,50,60,60,60,70,70,70,40,40,40,50,50,50,60,60,60,70,70,70,
  //   40,50,60,70,40,40,40,50,50,50,60,60,60,70,70,70,40,40,40,50,50,50,60,60,60,70,70,
  //   70,40,40,40,50,50,50,60,60,60,70,70,70,40,50,60,70,40,50,60,70,0,0,0,0,0,0,0,0,0,
  //   0,0,0,0,0,0,0,0,43,53,63,73,23,33,40,40,40,50,50,50,60,60,60,70,70,70,20,20,20,20,
  //   30,30,30,30,41,51,61,71,42,52,62,72,0,0,0,0,0,0,0,0,0,0,0,0,0,0,0,0,0,0,0,0,0,0,0,
  //   0,0,0,0,0,0,43,53,63,73,43,53,63,73,43,53,63,73,10,10,10,10,10,10,10,10,10,10,10,
  //   10,0,0,0,43,0,0,0,0,0,0,0,0,0,0,0,0,0,0,0,0,0,0,0,0,0,0,10,10,10,10,11,12,43,53,63,
  //   73,23,33,10,0,40,50,60,70,40,50,60,70,40,40,40,50,50,50,60,60,60,70,70,70,40,40,40,
  //   50,50,50,60,60,60,70,70,70,40,50,60,70,40,50,60,70,40,40,40,50,50,50,60,60,60,70,
  //   70,70,40,40,40,50,50,50,60,60,60,70,70,70,40,50,60,70,40,40,40,50,50,50,60,60,60,
  //   70,70,70,40,40,40,50,50,50,60,60,60,70,70,70,40,40,40,50,50,50,60,60,60,70,70,70,
  //   40,50,60,70,40,50,60,70,0,0,0,0,0,0,0,0,0,0,0,0,0,0,0,0,0,43,53,63,73,23,33,40,40,
  //   40,50,50,50,60,60,60,70,70,70,20,20,20,20,30,30,30,30,41,51,61,71,42,52,62,72,0,0,
  //   0,0,0,0,0,0,0,0,0,0,0,0,0,0,0,0,0,0,0,0,0,0,0,0,0,0,0,43,53,63,73,43,53,63,73,43,
  //   53,63,73,10,10,10,10,10,10,10,10,10,10,10,10,0,0,0,43,0,0,0,0,0,0,0,0,0,0,0,0,0,0,
  //   0,0,0,0,0,0,0,0,10,10,10,10,11,12,43,53,63,73,23,33,10,0,40,50,60,70,40,50,60,70,
  //   40,40,40,50,50,50,60,60,60,70,70,70,40,40,40,50,50,50,60,60,60,70,70,70,40,50,60,
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  //   contents of _2B (hex, n*v repeats v):
  //   4,4,4,4,4,4,4,4,4,4,4,4,4,4,4,4,4,4,4,4,4,4,4,4,4,4,4,4,4,4,4,4,4,4,4,4,4,4,4,4,4,
  //   4,4,4,4,4,4,4,4,4,4,4,5,6,7,4,4,4,4,4,4,4,4,4,30,30,30,30,34,34,34,34,38,38,38,38,
  //   30,30,30,30,34,34,34,34,38,38,38,38,4,4,4,32,48,48,48,24,4,4,4,4,4,4,4,4,4,4,4,4,
  //   4,4,4,4,4,4,2c,2c,2c,2c,2c,2c,2d,2d,2d,2d,2d,2d,37,4,4,4,4,4,4,4,4,4,4,4,4,4,4,4,
  //   4,4,4,4,4,4,4,4,4,4,4,4,4,4,4,4,4,4,4,4,4,4,4,4,4,4,4,4,4,4,4,4,4,4,4,4,4,4,4,4,4,
  //   4,4,4,4,4,4,4,4,4,4,4,4,4,4,4,4,4,4,4,4,4,4,4,4,4,4,4,4,4,4,4,4,4,4,4,4,4,4,4,4,4,
  //   4,4,4,4,4,4,4,4,4,4,4,4,4,4,4,4,4,4,4,4,4,4,4,4,4,4,4,4,4,4,4,4,4,4,4,4,4,4,4,4,4,
  //   4,4,4,4,4,4,4,4,4,4,4,4,4,4,4,4,4,4,4,4,4,4,4,4,4,4,4,4,4,4,4,4,4,4,4,4,4,4,4,4,4,
  //   4,4,5,6,7,4,4,4,4,4,4,4,4,4,30,30,30,30,34,34,34,34,38,38,38,38,30,30,30,30,34,34,
  //   34,34,38,38,38,38,4,4,4,32,48,48,48,24,4,4,4,4,4,4,4,4,4,4,4,4,4,4,4,4,4,4,2c,2c,
  //   2c,2c,2c,2c,2d,2d,2d,2d,2d,2d,37,4,4,4,4,4,4,4,4,4,4,4,4,4,4,4,4,4,4,4,4,4,4,4,4,
  //   4,4,4,4,4,4,4,4,4,4,4,4,4,4,4,4,4,4,4,4,4,4,4,4,4,4,4,4,4,4,4,4,4,4,4,4,4,4,4,4,4,
  //   4,4,4,4,4,4,4,4,4,4,4,4,4,4,4,4,4,4,4,4,4,4,4,4,4,4,4,4,4,4,4,4,4,4,4,4,4,4,4,4,4,
  //   4,4,4,4,4,4,4,4,4,4,4,4,4,4,4,4,4,4,4,4,4,4,4,4,4,4,4,4,4,4,4,4,4,4,4,4,4,4,4,4,4,
  //   4,4,4,4,4,4,4,4,4,4,4,4,4,4,4,4,4,4,4,4,4,4,4,4,4,4,4,4,4,4,4,4,4,4,5,6,7,4,4,4,4,
  //   4,4,4,4,4,30,30,30,30,34,34,34,34,38,38,38,38,30,30,30,30,34,34,34,34,38,38,38,38,
  //   4,4,4,32,48,48,48,24,4,4,4,4,4,4,4,4,4,4,4,4,4,4,4,4,4,4,2c,2c,2c,2c,2c,2c,2d,2d,
  //   2d,2d,2d,2d,37,4,4,4,4,4,4,4,4,4,4,4,4,4,4,4,4,4,4,4,4,4,4,4,4,4,4,4,4,4,4,4,4,4,
  //   4,4,4,4,4,4,4,4,4,4,4,4,4,4,4,4,4,4,4,4,4,4,4,4,4,4,4,4,4,4,4,4,4,4,4,4,4,4,4,4,4,
  //   4,4,4,4,4,4,4,4,4,4,4,4,4,4,4,4,4,4,4,4,4,4,4,4,4,4,4,4,4,4,4,4,4,4,4,4,4,4,4,4,4,
  //   4,4,4,4,4,4,4,4,4,4,4,4,4,4,4,4,4,4,4,4,4,4,4,4,4,4,4,4,4,4,4,4,4,4,4,4,4,4,4,4,4,
  //   4,4,4,4,4,4,4,4,4,4,4,4,4,4,4,4,4,4,4,4,4,4,4,4,4,5,6,7,4,4,4,4,4,4,4,4,4,30,30,30,
  //   30,34,34,34,34,38,38,38,38,30,30,30,30,34,34,34,34,38,38,38,38,4,4,4,32,48,48,48,
  //   24,4,4,4,4,4,4,4,4,4,4,4,4,4,4,4,4,4,4,2c,2c,2c,2c,2c,2c,2d,2d,2d,2d,2d,2d,37,4,4,
  //   4,4,4,4,4,4,4,4,4,4,4,4,4,4,4,4,4,4,4,4,4,4,4,4,4,4,4,4,4,4,4,4,4,4,4,4,4,4,4,4,4,
  //   4,4,4,4,4,4,4,4,4,4,4,4,4,4,4,4,4,4,4,4,4,4,4,4,4,4,4,4,4,4,4,4,4,4,4,4,4,4,4,4,4,
  //   4,4,4,4,4,4,4,4,4,4,4,4,4,4,4,4,4,4,4,4,4,4,4,4,4,4,4,4,4,4,4,4,4,4,4,4,4,4,4,4,4,
  //   4,4,4,4,4,4,4,4,4,4,4,4,4,4,4,4,4,4,4,4,4,4,4,4,4,4,4,4,4,4,4,4,4,4,4,4,4,4,4,4,4,
  //   4,4,4,4,4,4,4,4,4,4,4,4,4,4,4,5,6,7,4,4,4,4,4,4,4,4,4,30,30,30,30,34,34,34,34,38,
  //   38,38,38,30,30,30,30,34,34,34,34,38,38,38,38,4,4,4,32,48,48,48,24,4,4,4,4,4,4,4,4,
  //   4,4,4,4,4,4,4,4,4,4,2c,2c,2c,2c,2c,2c,2d,2d,2d,2d,2d,2d,37,4,4,4,4,4,4,4,4,4,4,4,
  //   4,4,4,4,4,4,4,4,4,4,4,4,4,4,4,4,4,4,4,4,4,4,4,4,4,4,4,4,4,4,4,4,4,4,4,4,4,4,4,4,4,
  //   4,4,4,4,4,4,4,4,4,4,4,4,4,4,4,4,4,4,4,4,4,4,4,4,4,4,4,4,4,4,4,4,4,4,4,4,4,4,4,4,4,
  //   4,4,4,4,4,4,4,4,4,4,4,4,4,4,4,4,4,4,4,4,4,4,4,4,4,4,4,4,4,4,4,4,4,4,4,4,4,4,4,4,4,
  //   4,4,4,4,4,4,4,4,4,4,4,4,4,4,4,4,4,4,4,4,4,4,4,4,4,4,4,4,4,4,4,4,4,4,4,4,4,4,4,4,4,
  //   4,4,4,4,4,4,5,6,7,4,4,4,4,4,4,4,4,4,30,30,30,30,34,34,34,34,38,38,38,38,30,30,30,
  //   30,34,34,34,34,38,38,38,38,4,4,4,32,48,48,48,24,4,4,4,4,4,4,4,4,4,4,4,4,4,4,4,4,4,
  //   4,2c,2c,2c,2c,2c,2c,2d,2d,2d,2d,2d,2d,37,4,4,4,4,4,4,4,4,4,4,4,4,4,4,4,4,4,4,4,4,
  //   4,4,4,4,4,4,4,4,4,4,4,4,4,4,4,4,4,4,4,4,4,4,4,4,4,4,4,4,4,4,4,4,4,4,4,4,4,4,4,4,4,
  //   4,4,4,4,4,4,4,4,4,4,4,4,4,4,4,4,4,4,4,4,4,4,4,4,4,4,4,4,4,4,4,4,4,4,4,4,4,4,4,4,4,
  //   4,4,4,4,4,4,4,4,4,4,4,4,4,4,4,4,4,4,4,4,4,4,4,4,4,4,4,4,4,4,4,4,4,4,4,4,4,4,4,4,4,
  //   4,4,4,4,4,4,4,4,4,4,4,4,4,4,4,4,4,4,4,4,4,4,4,4,4,4,4,4,4,4,4,4,4,4,4,4,4,4,5,6,7,
  //   4,4,4,4,4,4,4,4,4,30,30,30,30,34,34,34,34,38,38,38,38,30,30,30,30,34,34,34,34,38,
  //   38,38,38,4,4,4,32,48,48,48,24,4,4,4,4,4,4,4,4,4,4,4,4,4,4,4,4,4,4,2c,2c,2c,2c,2c,
  //   2c,2d,2d,2d,2d,2d,2d,37,4,4,4,4,4,4,4,4,4,4,4,4,4,4,4,4,4,4,4,4,4,4,4,4,4,4,4,4,4,
  //   4,4,4,4,4,4,4,4,4,4,4,4,4,4,4,4,4,4,4,4,4,4,4,4,4,4,4,4,4,4,4,4,4,4,4,4,4,4,4,4,4,
  //   4,4,4,4,4,4,4,4,4,4,4,4,4,4,4,4,4,4,4,4,4,4,4,4,4,4,4,4,4,4,4,4,4,4,4,4,4,4,4,4,4,
  //   4,4,4,4,4,4,4,4,4,4,4,4,4,4,4,4,4,4,4,4,4,4,4,4,4,4,4,4,4,4,4,4,4,4,4,4,4,4,4,4,4,
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endmodule
