// Digital circuit GPR.dig as structural Verilog
module GPR (
  input  [3:0] Control,
  output [7:0] MAIN,
  output [7:0] LHS,
  output [7:0] RHS,
  output [7:0] I
);

  _74541 _74541_1 (
    .pin1(Control[1]), .pin2(I[0]), .pin3(I[1]), .pin4(I[2]), .pin5(I[3]), .pin6(I[4]), .pin7(I[5]),
    .pin8(I[6]), .pin9(I[7]), .pin10(1'b0), .pin11(MAIN[7]), .pin12(MAIN[6]), .pin13(MAIN[5]),
    .pin14(MAIN[4]), .pin15(MAIN[3]), .pin16(MAIN[2]), .pin17(MAIN[1]), .pin18(MAIN[0]), .pin19(1'b0),
    .pin20(1'b1));
  _74541 _74541_2 (
    .pin1(Control[2]), .pin2(I[0]), .pin3(I[1]), .pin4(I[2]), .pin5(I[3]), .pin6(I[4]), .pin7(I[5]),
    .pin8(I[6]), .pin9(I[7]), .pin10(1'b0), .pin11(LHS[7]), .pin12(LHS[6]), .pin13(LHS[5]), .pin14(LHS[4]),
    .pin15(LHS[3]), .pin16(LHS[2]), .pin17(LHS[1]), .pin18(LHS[0]), .pin19(1'b0), .pin20(1'b1));
  _74574 _74574_1 (
    .pin1(1'b0), .pin2(MAIN[0]), .pin3(MAIN[1]), .pin4(MAIN[2]), .pin5(MAIN[3]), .pin6(MAIN[4]),
    .pin7(MAIN[5]), .pin8(MAIN[6]), .pin9(MAIN[7]), .pin10(1'b0), .pin11(Control[0]), .pin12(I[7]),
    .pin13(I[6]), .pin14(I[5]), .pin15(I[4]), .pin16(I[3]), .pin17(I[2]), .pin18(I[1]), .pin19(I[0]),
    .pin20(1'b1));
  _74541 _74541_3 (
    .pin1(Control[3]), .pin2(I[0]), .pin3(I[1]), .pin4(I[2]), .pin5(I[3]), .pin6(I[4]), .pin7(I[5]),
    .pin8(I[6]), .pin9(I[7]), .pin10(1'b0), .pin11(RHS[7]), .pin12(RHS[6]), .pin13(RHS[5]), .pin14(RHS[4]),
    .pin15(RHS[3]), .pin16(RHS[2]), .pin17(RHS[1]), .pin18(RHS[0]), .pin19(1'b0), .pin20(1'b1));

  // Other names for the same wires on the sheet: MainBus[7:0] = MAIN; LHSBus[7:0] = LHS; Reg[7:0] = I;
  //   RHSBus[7:0] = RHS; Load = Control[0]; A_Main = Control[1]; A_LHS = Control[2]; A_RHS = Control[3]

  // Notes on the sheet:
  //   Control: 0: Load
  //   1: Assert Main
  //   2: Assert LHS
  //   3: Assert RHS, default 15
endmodule
