// Digital circuit Fetch.dig as structural Verilog
module Fetch (
  input  [7:0] MEM,
  input  [1:0] Control,
  input  [6:0] Flags,
  input  Clock,
  output [7:0] PipeOut,
  output [1:0] PCRA
);

  wire [7:0] register_1_q;

  Register #(.Bits(8)) register_1 (.D(MEM), .C(Clock), .en(1'b1), .Q(register_1_q));
  Multiplexer #(.Selector_Bits(2), .Bits(8)) multiplexer_1 (
    .sel(Control), .in_0(MEM), .in_1({8{1'b0}}), .in_2({8{1'b0}}), .in_3(register_1_q), .out(PipeOut));

  assign PCRA = {Control[1], Flags[5]};

  // Notes on the sheet:
  //   Control: 0: FetchSurpress
  //   1: BusRequest
  //   Flags: 0: Overflow
  //   1: Sign
  //   2: Zero
  //   3: CarryA
  //   4: CarryL
  //   5: PCRA Flip
  //   6: Reset
  //   PCRA: 0,1: Inc PCRA0,1
endmodule
