// Digital circuit Stage 1.dig as structural Verilog
module Stage_1 (
  input  [1:0] Control,
  input  [6:0] Flags,
  input  Clock,
  input  [7:0] PipeIn,
  input  [6:0] Xfer,
  input  [3:0] ALU_Bus,
  output [3:0] ALU_Ops,
  output [7:0] PipeOut,
  output Fetch_suppress
);

  wire nand_1_out;
  wire [7:0] register_1_q;
  wire [15:0] _1A_d;

  ROM #(.AddrBits(15), .Bits(8)) _1A (.A({Flags, PipeIn}), .sel(1'b1), .D(_1A_d[7:0]));
  ROM #(.AddrBits(15), .Bits(8)) _1B (.A({Flags, PipeIn}), .sel(1'b1), .D(_1A_d[15:8]));
  nand nand_1 (nand_1_out, Control[0], Control[1]);
  Register #(.Bits(8)) register_1 (.D(PipeIn), .C(Clock), .en(1'b1), .Q(register_1_q));
  assign PipeOut = nand_1_out ? register_1_q : 8'bz;  // Driver driver_1
  Register #(.Bits(16)) register_2 (.D(_1A_d), .C(Clock), .en(1'b1), .Q({Fetch_suppress, Xfer, ALU_Ops, ALU_Bus}));
  PullDown #(.Bits(8)) pulldown_1 (.out(PipeOut));

  // Other names for the same wires on the sheet: ControlIn[1:0] = Control

  // Notes on the sheet:
  //   ALU_Ops: 0: ALUOP0
  //   1: ALUOP1
  //   2: ALUOP2
  //   3: ALUOP3
  //   Control: 0: FetchSurpress
  //   1: BusRequest
  //   Flags: 0: Overflow
  //   1: Sign
  //   2: Zero
  //   3: CarryA
  //   4: CarryL
  //   5: PCRA Flip
  //   6: Reset
  //   Fetch_suppress: Fetch suppress
  //   Xfer: 000xxxx: Assert Xfer 0-2
  //   xxx0000: Load Xfer Dec 0-3
  //   ALU_Bus: 0,1: LHS0,1
  //   2,3: RHS0,1
endmodule
