// Digital circuit Stage 2.dig as structural Verilog
module Stage_2 (
  input  [6:0] Flags,
  input  Clock,
  input  [7:0] PipeIn,
  input  [7:0] Main,
  input  [1:0] SPSIDI,
  input  [2:0] Addr,
  output Bus_Request,
  output PCRA_Flip,
  output Break
);

  wire [7:0] _28c256_1_p11, _28c256_2_p11, _74574_1_pin19;

  _74574 _74574_1 (
    .pin1(1'b0), .pin2(PipeIn[0]), .pin3(PipeIn[1]), .pin4(PipeIn[2]), .pin5(PipeIn[3]), .pin6(PipeIn[4]),
    .pin7(PipeIn[5]), .pin8(PipeIn[6]), .pin9(PipeIn[7]), .pin10(1'b0), .pin11(Clock),
    .pin12(_74574_1_pin19[7]), .pin13(_74574_1_pin19[6]), .pin14(_74574_1_pin19[5]),
    .pin15(_74574_1_pin19[4]), .pin16(_74574_1_pin19[3]), .pin17(_74574_1_pin19[2]),
    .pin18(_74574_1_pin19[1]), .pin19(_74574_1_pin19[0]), .pin20(1'b1));
  // _28c256 _28c256_1: pin names not known; wires that end beside it: Flags[6], Flags[4], _74574_1_pin19[7], _74574_1_pin19[6], _74574_1_pin19[5], _74574_1_pin19[4], _74574_1_pin19[3], _74574_1_pin19[2], _74574_1_pin19[1], _74574_1_pin19[0], _28c256_1_p11[0], _28c256_1_p11[1], _28c256_1_p11[2], 1'b0, 1'b1, 1'b1, Flags[5], Flags[0], Flags[1], Flags[3], 1'b0, Flags[2], 1'b0, _28c256_1_p11[7]
  _74574 _74574_2 (
    .pin1(1'b0), .pin2(_28c256_1_p11[0]), .pin3(_28c256_1_p11[1]), .pin4(_28c256_1_p11[2]),
    .pin5(_28c256_1_p11[3]), .pin6(_28c256_1_p11[4]), .pin7(_28c256_1_p11[5]), .pin8(_28c256_1_p11[6]),
    .pin9(_28c256_1_p11[7]), .pin10(1'b0), .pin11(Clock), .pin12(Main[7]), .pin13(Main[6]), .pin14(Main[5]),
    .pin15(Main[4]), .pin16(Main[3]), .pin17(Main[2]), .pin18(Main[1]), .pin19(Main[0]), .pin20(1'b1));
  // _28c256 _28c256_2: pin names not known; wires that end beside it: Flags[6], Flags[4], _74574_1_pin19[7], _74574_1_pin19[6], _74574_1_pin19[5], _74574_1_pin19[4], _74574_1_pin19[3], _74574_1_pin19[2], _74574_1_pin19[1], _74574_1_pin19[0], _28c256_2_p11[0], _28c256_2_p11[1], _28c256_2_p11[2], 1'b0, 1'b1, 1'b1, Flags[5], Flags[0], Flags[1], Flags[3], 1'b0, Flags[2], 1'b0, _28c256_2_p11[7]
  _74574 _74574_3 (
    .pin1(1'b0), .pin2(_28c256_2_p11[0]), .pin3(_28c256_2_p11[1]), .pin4(_28c256_2_p11[2]),
    .pin5(_28c256_2_p11[3]), .pin6(_28c256_2_p11[4]), .pin7(_28c256_2_p11[5]), .pin8(_28c256_2_p11[6]),
    .pin9(_28c256_2_p11[7]), .pin10(1'b0), .pin11(Clock), .pin12(Break), .pin13(PCRA_Flip),
    .pin14(Bus_Request), .pin15(Addr[2]), .pin16(Addr[1]), .pin17(Addr[0]), .pin18(SPSIDI[1]),
    .pin19(SPSIDI[0]), .pin20(1'b1));

  // Other names for the same wires on the sheet: ControlOut[15:0] = {Break, PCRA_Flip, Bus_Request, Addr, SPSIDI, Main}

  // Notes on the sheet:
  //   Flags: 0: Overflow
  //   1: Sign
  //   2: Zero
  //   3: CarryA
  //   4: CarryL
  //   5: PCRA Flip
  //   6: Reset
  //   Bus_Request: 1: PCRA Flip
  //   2: Break
  //   Main: 0-3: Assert A-D
  //   4-7: Load A-D
  //   SPSIDI: 0,1: Inc SPSIDI0,1
  //   Addr: 0,2: Sel 1-2
endmodule
