// Digital circuit System.dig as structural Verilog
module System (
  input  Clock,
  input  Reset
);

  wire and_1_out, core_1_r_nw;
  wire [7:0] blockramdualport_1_d, core_1_d_out, multiplexer_1_out, multiplexer_2_out, rom_1_d;
  wire [13:0] core_1_addr;
  wire [15:14] core_1_addr_2;

  Core core_1 (
    .R_nW(core_1_r_nw), .Addr({core_1_addr_2, core_1_addr}), .D_OUT(core_1_d_out), .D_IN(multiplexer_1_out),
    .Clock(Clock), .nReset(Reset));
  and and_1 (and_1_out, ~core_1_addr_2[15], core_1_addr_2[14]);  // And
  BlockRAMDualPort #(.AddrBits(15), .Bits(8)) blockramdualport_1 (
    .A({core_1_addr_2[14], core_1_addr}), .Din(core_1_d_out), .str(core_1_r_nw), .C(Clock),
    .D(blockramdualport_1_d));
  ROM #(.AddrBits(14), .Bits(8)) rom_1 (.A(core_1_addr), .sel(1'b1), .D(rom_1_d));
  Terminal terminal_1 (.Data(core_1_d_out), .Clock(Clock), .Load(and_1_out));
  Multiplexer #(.Bits(8)) multiplexer_1 (
    .sel(core_1_addr_2[15]), .in_0(multiplexer_2_out), .in_1(blockramdualport_1_d), .out(multiplexer_1_out));
  Multiplexer #(.Bits(8)) multiplexer_2 (
    .sel(core_1_addr_2[14]), .in_0(rom_1_d), .in_1({8{1'b0}}), .out(multiplexer_2_out));

  // Notes on the sheet:
  //   Clock: Hz: 100
  //   Reset: default 1
  //   contents of rom_1 (hex, n*v repeats v):
  //   0,5,33,6,0,27,5,14,6,0,5c,0,0,0,5,1,6,0,5f,60,2a,72,76,77,0,5,22,6,0,29,5,2d,6,0,
  //   5b,fc,5f,65,5,0,6,40,54,5f,71,7d,7c,78,29,5e,0,48,65,6c,6c,6f,20,57,6f,72,6c,64,21,
  //   a
endmodule
