// Digital circuit Terminal.dig as structural Verilog
module Terminal (
  input  [7:0] Data,
  input  Clock,
  input  Load
);

  wire not_1_out;

  not not_1 (not_1_out, Clock);
  Terminal terminal_1 (.D(Data), .C(not_1_out), .en(Load));
endmodule
