// Digital circuit Transfer Register.dig as structural Verilog
module Transfer_Register (
  input  [7:0] Control,
  input  [15:0] XFER,
  input  Clock,
  output [7:0] MAIN,
  output [15:0] ADDR,
  output [15:0] I
);

  wire or_1_out, or_2_out;
  wire [7:0] multiplexer_1_out, multiplexer_2_out;

  or or_1 (or_1_out, Control[0], Control[4]);
  or or_2 (or_2_out, Control[6], Control[0]);
  Multiplexer #(.Bits(8)) multiplexer_1 (.sel(Control[0]), .in_0(MAIN), .in_1(XFER[7:0]), .out(multiplexer_1_out));
  Multiplexer #(.Bits(8)) multiplexer_2 (.sel(Control[0]), .in_0(MAIN), .in_1(XFER[15:8]), .out(multiplexer_2_out));
  Register #(.Bits(8)) TL (.D(multiplexer_1_out), .C(Clock), .en(or_1_out), .Q(I[7:0]));
  Register #(.Bits(8)) TH (.D(multiplexer_2_out), .C(Clock), .en(or_2_out), .Q(I[15:8]));
  assign XFER = Control[2] ? I : 16'bz;  // Driver driver_1
  assign ADDR = Control[1] ? I : 16'bz;  // Driver driver_2
  assign MAIN = Control[5] ? I[7:0] : 8'bz;  // Driver driver_3
  assign MAIN = Control[7] ? I[15:8] : 8'bz;  // Driver driver_4

  // Notes on the sheet:
  //   ADDR: Addr Bus
  //   Control: 0: RegTX Load
  //   1: RegTX Assert Addr
  //   2: RegTX Assert Xfer
  //   3: RegTX Assert Mode
  //   4: RegTL Load
  //   5: RegTL Assert
  //   6: RegTH Load
  //   7: RegTH Assert, default 255
endmodule
